# Fritzing sketch scheme (saved by Fritzing 1.0.5)

parts:
  Grove1 = TM1637 7segment 4digit display
  KY-1 = Keyes Relay [package=THT]
  U1 = LuaNode32 / ESP32 [part_number=ESP32S-PIN30]
  RE1 = KY-040 Rotary encoder [package=THT]
  KY-2 = Keyes Relay [package=THT]
  LED1 = smd LED [color="Red (633nm)" package="1206 [SMD]"]
  LED2 = smd LED [color="Red (633nm)" package="1206 [SMD]"]
  S1 = Pushbutton [package="[THT]"]
  R1 = Resistor [tolerance=±5% power=0.25W resistance=220 package=THT]
  Part1 = ACS712 Low Current Sensor Board v12
  HLK-PM1 = HLK-PM01
  J2 = Screw terminal - 2 pins [package=THT]
  J1 = Screw terminal - 2 pins [package=THT]
  J3 = Screw terminal - 2 pins [package=THT]
  DS1 = DS18B20 1-Wire Temperature Sensor [part_number=DS18B20]
  R2 = Resistor [tolerance=±5% power=0.25W resistance=220 package=THT]
  R3 = Resistor [tolerance=±5% power=0.25W resistance=1k package=THT]
  R4 = Resistor [tolerance=±5% power=0.25W resistance=1k package=THT]
  R5 = Resistor [tolerance=±5% power=0.25W resistance=1k package=THT]

nets:
  VCC: Grove1.Vcc, KY-1.power, U1.Vin, RE1.Vcc, KY-2.power, Part1.5V, HLK-PM1.+Vo, DS1.VDD
  GND: Grove1.GND, KY-1.ground, U1.GND, RE1.GND, KY-2.ground, S1.Pin_3, S1.Pin_4, R1.Pin_1, Part1.GND, HLK-PM1.-Vo, DS1.GND, R2.Pin_1, R5.Pin_0
  N1: Grove1.DIO, U1.D33
  N2: Grove1.CLK, U1.D32
  N3: KY-1.signal, U1.D13, LED1.anode
  N4: KY-1.C, J3.pin1
  N5: KY-1.NO, Part1.IP-
  N6: U1.D35, R3.Pin_0, R4.Pin_1
  N7: U1.D25, RE1.SW
  N8: U1.D26, RE1.DT
  N9: U1.D27, RE1.CLK
  N10: U1.D12, KY-2.signal, LED2.anode
  N11: U1.D15, DS1.DQ
  N12: U1.D4, S1.Pin_1
  N13: KY-2.C, J2.pin1
  N14: KY-2.NO, J2.pin2
  N15: LED1.cathode, R1.Pin_0
  N16: LED2.cathode, R2.Pin_0
  N17: Part1.VO, R3.Pin_1
  N18: Part1.IP+, J3.pin2
  N19: HLK-PM1.AC#0, J1.pin2
  N20: HLK-PM1.AC#1, J1.pin1
  N21: R4.Pin_0, R5.Pin_1

notes:
  pump
  heater
  load limeted by relay. If you need more load use AC contactor.
  Currency sensor for check dry running. Disable (in programm) if use contactor.

custom parts:
  Keyes Relay: The Keyes 5V relay module is suitable for SCM development, home appliance control. It uses a 5V~12V TIL control signal which can control DC / AC signal.
  LuaNode32 / ESP32: New Image for LuaNode32 DOIT ESP32 DEVKIT V1. Base parts from LuaNode32 / ESP32 ESP32 based LuaNode32 by G.Noorlander DOIT Esp32 DevKit v1 (30 pins long, 11 pins width) by Werner Rothschopf (modified by vanepp Dec 2018)
  KY-040 Rotary encoder: KY-040 Rotary Encoder with switch on breakout borad from AZ Delivery
